# Fritzing sketch vloradio (saved by Fritzing 0.9.3b)
breadboards: 2

parts:
  Raspberry_Pi1 = Raspberry Pi 2
  U1 = LCD-16X2 [package=lcd-16x2]
  R1 = Trimmer Potentiometer [maximum_resistance=2kΩ package=THT]
  S1 = Momentary Switch [package=tactile-pth]
  RE1 = Rotary Encoder [package=THT]
  S2 = Momentary Switch [package=tactile-pth]
  S3 = Momentary Switch [package=tactile-pth]
  S4 = Momentary Switch [package=tactile-pth]
  S5 = Momentary Switch [package=tactile-pth]
  S6 = Momentary Switch [package=tactile-pth]
  C1 = Electrolytic Capacitor [capacitance=0.47mF voltage=16V package="200 mil [THT, electrolytic]"]
  DHT1 = DHT22 Humidity and Temperature Sensor
  IR1 = TSOP312.., 314.. [package=THT]
  R2 = Trimmer Potentiometer [maximum_resistance=10kΩ package=THT]
  C2 = Electrolytic Capacitor [capacitance=0.47mF voltage=16V package="200 mil [THT, electrolytic]"]

nets:
  3V3: Raspberry_Pi1.3v3, C1.+, DHT1.VDD, IR1.Vs
  N1: Raspberry_Pi1.GPIO17, RE1.EncoderPinA
  N2: Raspberry_Pi1.GPIO27, IR1.Data
  N3: Raspberry_Pi1.GPIO22, S4.1
  N4: Raspberry_Pi1.GPIO5, RE1.EncoderPinB
  N5: Raspberry_Pi1.GPIO6, S1.1
  N6: Raspberry_Pi1.GPIO13, U1.DB5
  N7: Raspberry_Pi1.GPIO19, U1.DB4
  N8: Raspberry_Pi1.GPIO26, U1.RS
  N9: Raspberry_Pi1.GPIO21, U1.DB6
  N10: Raspberry_Pi1.GPIO20, U1.E
  N11: Raspberry_Pi1.GPIO16, U1.DB7
  N12: Raspberry_Pi1.GPIO12, S2.1
  N13: Raspberry_Pi1.GPIO25, DHT1.DATA
  N14: Raspberry_Pi1.GPIO24, S3.1
  N15: Raspberry_Pi1.GPIO23, S5.1
  N16: Raspberry_Pi1.GPIO18, S6.1
  GND: Raspberry_Pi1.GND, U1.VSS, U1.R_W, U1.K, R1.leg1, S1.4, RE1.EncoderPinC, S2.4, S3.4, S4.4, S5.4, S6.4, C1.-, DHT1.GND, IR1.GND, R2.leg1, C2.-
  5V: Raspberry_Pi1.5V, U1.VDD, R1.leg2, R2.leg2, C2.+
  N17: U1.VO, R1.wiper
  N18: U1.A, R2.wiper

notes:
  5VDC Rail
  3V3 DC Rail
  Broadcom GPIO |
  # Pin number number | Function
  # ----------------------------------------------------------
  # 6 | Tap=Redraw Now Playing / Hold=Shutdown
  # 12 | Tap=Display Temp / Hold=Skip Track
  # 16 | Tap=Love song / Hold=Ban song
  # 18 | Tap=Mute/Unmute / Hold=Return to sane volume level
  # 19 | Tap=Play/Pause / Hold=Tired of Song
  # 20 | Tap=Menu/Select / Hold=Go back
  # -----------------------------------------------------------
  All Pins have internal pull up's enabled and are input pins
  Rotary Encoder Controls the Volume and Menu
